# Fritzing sketch conexion (saved by Fritzing 0.9.3b)
breadboards: 1

parts:
  Componente1 = Arduino Uno (Rev3)
  U1 = POT [package=pot_mammoth]
  R1 = Photocell (LDR) [package=THT]
  R2 = Resistor [tolerance=±5% resistance=10k package=THT]
  R3 = Resistor [tolerance=±5% resistance=220 package=THT]
  Componente2 = HC-SR501 Body Sensor Module
  U2 = POT [package=pot_mammoth]
  LED2 = LED - 5mm [color="Red (633nm)" package="5 mm [THT]"]

nets:
  N1: Componente1.A0, U1.A
  N2: Componente1.A1, U2.A
  N3: Componente1.A2, R1.pin_1, R2.Pin_0
  N4: Componente1.D11_PWM/MOSI, LED2.anode
  GND: Componente1.GND, U1.E, R2.Pin_1, R3.Pin_1, Componente2.GND, U2.E
  N5: Componente1.D3_PWM, Componente2.OUT
  5V: Componente1.5V, U1.S, R1.pin_0, Componente2.VCC, U2.S
  N6: R3.Pin_0, LED2.cathode

custom parts:
  HC-SR501 Body Sensor Module: Pyroelectric Infrared PIR Motion Sensor Detector Module
